# Fritzing sketch ArduinoWorkshop (saved by Fritzing 0.9.9b)
breadboards: 1

parts:
  Uno = Arduino Uno (Rev3)
  LED1 = LED - 5mm [color="Red (633nm)" current=0.030 package="5 mm [THT]"]
  R1 = Resistor [tolerance=±5% power=0.25 resistance=220 package=THT]
  SG1 = Buzzer 12mm [package=buzzer-ccv]
  M1 = fc-51 [package=THT]

nets:
  N1: Uno.D12/MISO, M1.pin1
  N2: Uno.GND, R1.Pin_0, SG1.1, M1.pin2
  N3: Uno.D6_PWM, LED1.anode
  N4: Uno.D7, SG1.2
  N5: Uno.5V, M1.pin3
  N6: LED1.cathode, R1.Pin_1
